// Logisim project LAB1_CSE231.circ as structural Verilog: 4 circuits, main circuit main
module main (
  input  in_1,
  input  in_2,
  input  in_3,
  output out_4
);

  wire ic7404_1_out_7, ic7404_1_out_8, ic7408_1_out_9, ic7408_1_out_10, ic7408_1_out_11, ic7432_1_out_9;

  IC7404 ic7404_1 (
    .in_1(in_1), .in_2(in_2), .out_7(ic7404_1_out_7), .out_8(ic7404_1_out_8));  // open: in_3, in_4, in_5, in_6, out_9, out_10, out_11, out_12
  IC7408 ic7408_1 (
    .in_1(ic7404_1_out_7), .in_2(in_3), .in_3(in_1), .in_4(ic7404_1_out_8), .in_5(in_2), .in_6(in_3),
    .out_9(ic7408_1_out_9), .out_10(ic7408_1_out_10), .out_11(ic7408_1_out_11));  // open: in_7, in_8, out_12
  IC7432 ic7432_1 (
    .in_1(ic7408_1_out_9), .in_2(ic7408_1_out_10), .in_3(ic7432_1_out_9), .in_4(ic7408_1_out_11),
    .out_9(ic7432_1_out_9), .out_10(out_4));  // open: in_5, in_6, in_7, in_8, out_11, out_12
endmodule

module IC7408 (
  input  in_1,
  input  in_2,
  input  in_3,
  input  in_4,
  input  in_5,
  input  in_6,
  input  in_7,
  input  in_8,
  output out_9,
  output out_10,
  output out_11,
  output out_12
);

  and and_1 (out_9, in_1, in_2);
  and and_2 (out_10, in_3, in_4);
  and and_3 (out_11, in_5, in_6);
  and and_4 (out_12, in_7, in_8);
endmodule

module IC7404 (
  input  in_1,
  input  in_2,
  input  in_3,
  input  in_4,
  input  in_5,
  input  in_6,
  output out_7,
  output out_8,
  output out_9,
  output out_10,
  output out_11,
  output out_12
);

  not not_1 (out_7, in_1);
  not not_2 (out_8, in_2);
  not not_3 (out_9, in_3);
  not not_4 (out_10, in_4);
  not not_5 (out_11, in_5);
  not not_6 (out_12, in_6);
endmodule

module IC7432 (
  input  in_1,
  input  in_2,
  input  in_3,
  input  in_4,
  input  in_5,
  input  in_6,
  input  in_7,
  input  in_8,
  output out_9,
  output out_10,
  output out_11,
  output out_12
);

  or or_1 (out_9, in_1, in_2);
  or or_2 (out_10, in_3, in_4);
  or or_3 (out_11, in_5, in_6);
  or or_4 (out_12, in_7, in_8);
endmodule
